// Logisim project ALU.circ as structural Verilog: 5 circuits, main circuit main
module main (
  input  Cin,
  input  [19:0] A,
  input  [19:0] B,
  input  [4:0] shamt,
  input  [1:0] ALU_OP,
  input  [2:0] func,
  output [19:0] \output ,
  output overflow,
  output [19:0] output_2,
  output zero,
  output negative
);

  wire adder_2_cout, Addovf, not_1_out, Subovf;
  wire [2:0] select;
  wire [19:0] adder_1_out, adder_2_out, and_1_out, n20_bit_sll_1_output, n20_bit_slt_1_out_3,
       n20_bit_srl_1_output, not_2_out, or_1_out;

  not not_1 (not_1_out, Cin);
  assign not_2_out = ~B;  // NOT_Gate not_2, 20 bits wide
  assign \output  = ~(A | B);  // NOR_Gate nor_1, 20 bits wide
  assign or_1_out = A | B;  // OR_Gate or_1, 20 bits wide
  Adder #(.width(20)) adder_1 (.a(A), .b(B), .out(adder_1_out), .cin(Cin), .cout(Addovf));
  _20_bit_SRL u_20_bit_srl_1 (.Input(A), .shamt(shamt), .\output (n20_bit_srl_1_output));
  _20_bit_SLT u_20_bit_slt_1 (.A(A), .B(B), .out_3(n20_bit_slt_1_out_3));
  _20_bit_SLL u_20_bit_sll_1 (.inputs(A), .shamt(shamt), .\output (n20_bit_sll_1_output));
  Adder #(.width(20)) adder_2 (.a(A), .b(not_2_out), .out(adder_2_out), .cin(not_1_out), .cout(adder_2_cout));
  assign and_1_out = A & B;  // AND_Gate and_1, 20 bits wide
  not not_3 (Subovf, adder_2_cout);
  Multiplexer #(.select(3), .width(20), .enable("false")) multiplexer_1 (
    .in0(\output ), .in1(or_1_out), .in2(adder_1_out), .in3(n20_bit_srl_1_output), .in4(n20_bit_slt_1_out_3),
    .in5(n20_bit_sll_1_output), .in6(adder_2_out), .in7(and_1_out), .out(output_2), .sel(select));
  ALU_control_unit alu_control_unit_1 (
    .FUNC(func), .ALUOP(ALU_OP), .PIN_0(select[0]), .PIN_1(select[1]), .PIN_2(select[2]));  // open: NOR
  Comparator #(.width(20)) comparator_1 (.a(output_2), .b({20{1'b0}}), .eq(zero), .lt(negative));  // open: gt
  Multiplexer #(.select(3), .enable("false")) multiplexer_2 (
    .in0(1'b0), .in1(1'b0), .in2(Addovf), .in3(1'b0), .in4(1'b0), .in5(1'b0), .in6(Subovf), .in7(1'b0),
    .out(overflow), .sel(select));
endmodule

module _20_bit_SRL (
  input  [19:0] Input,
  input  [4:0] shamt,
  output [19:0] \output 
);

  Shifter #(.width(20), .shift("lr")) shifter_1 (.in(Input), .\dist (shamt), .out(\output ));
endmodule

module _20_bit_SLT (
  input  [19:0] A,
  input  [19:0] B,
  output [19:0] out_3
);

  wire comparator_1_lt;

  Comparator #(.width(20)) comparator_1 (.a(A), .b(B), .lt(comparator_1_lt));  // open: gt, eq
  assign out_3 = {{19{1'b0}}, comparator_1_lt};  // Bit_Extender bit_extender_1
endmodule

module _20_bit_SLL (
  input  [19:0] inputs,
  input  [4:0] shamt,
  output [19:0] \output 
);

  Shifter #(.width(20)) shifter_1 (.in(inputs), .\dist (shamt), .out(\output ));
endmodule

module ALU_control_unit (
  input  [1:0] ALUOP,
  input  [2:0] FUNC,
  output NOR,
  output PIN_0,
  output PIN_1,
  output PIN_2
);

  wire and_1_out, and_2_out, and_4_out, and_5_out, and_6_out, and_7_out, and_8_out, decoder_1_out0,
       decoder_1_out1, decoder_1_out2, decoder_1_out3, decoder_1_out4, decoder_1_out5, decoder_1_out6,
       decoder_1_out7, decoder_2_out0, decoder_2_out1, decoder_2_out2, decoder_2_out3, or_1_out, or_2_out;

  Decoder #(.select(3), .enable("false")) decoder_1 (
    .out0(decoder_1_out0), .out1(decoder_1_out1), .out2(decoder_1_out2), .out3(decoder_1_out3),
    .out4(decoder_1_out4), .out5(decoder_1_out5), .out6(decoder_1_out6), .out7(decoder_1_out7), .sel(FUNC));
  Decoder #(.select(2), .enable("false")) decoder_2 (
    .out0(decoder_2_out0), .out1(decoder_2_out1), .out2(decoder_2_out2), .out3(decoder_2_out3), .sel(ALUOP));
  and and_1 (and_1_out, decoder_2_out2, decoder_1_out2);
  and and_2 (and_2_out, decoder_2_out2, decoder_1_out6);
  and and_3 (NOR, decoder_2_out2, decoder_1_out0);
  and and_4 (and_4_out, decoder_2_out2, decoder_1_out1);
  or or_1 (or_1_out, and_1_out, decoder_2_out1);
  and and_5 (and_5_out, decoder_2_out2, decoder_1_out3);
  and and_6 (and_6_out, decoder_2_out2, decoder_1_out4);
  and and_7 (and_7_out, decoder_2_out2, decoder_1_out5);
  or or_2 (or_2_out, and_2_out, decoder_2_out0);
  and and_8 (and_8_out, decoder_2_out2, decoder_1_out7);
  or or_3 (PIN_0, and_4_out, and_5_out, and_7_out, and_8_out);
  or or_4 (PIN_1, or_1_out, and_5_out, or_2_out, and_8_out);
  or or_5 (PIN_2, and_6_out, and_7_out, or_2_out, and_8_out);

  // Notes on the sheet:
  //   OR
  //   ADD
  //   SRL
  //   SLT
  //   SLL
  //   SUB
  //   AND
  //   BNE/SUB/BEQ
endmodule
