// Logisim project CSE_332_Group_11_20_bit_CPU(final).circ as structural Verilog: 10 circuits, main circuit main
module main (
  input  [19:0] A,
  input  [19:0] B,
  input  [1:0] shamt,
  input  [1:0] ALU_OP,
  input  [2:0] func,
  output overflow,
  output [19:0] \output ,
  output zero,
  output not_equal
);

  wire adder_2_cout, Addovf, comparator_2_gt, comparator_2_lt, Subovf;
  wire [2:0] select;
  wire [19:0] adder_1_out, adder_2_out, and_1_out, n20_bit_sll_1_output, n20_bit_slt_1_out_3,
       n20_bit_srl_1_output, nor_1_out, not_1_out, or_1_out;

  assign not_1_out = ~B;  // NOT_Gate not_1, 20 bits wide
  assign nor_1_out = ~(A | B);  // NOR_Gate nor_1, 20 bits wide
  assign or_1_out = A | B;  // OR_Gate or_1, 20 bits wide
  Adder #(.width(20)) adder_1 (.a(A), .b(B), .out(adder_1_out), .cin(1'b0), .cout(Addovf));
  _20_bit_SRL u_20_bit_srl_1 (.Input(A), .shamt(shamt), .\output (n20_bit_srl_1_output));
  _20_bit_SLT u_20_bit_slt_1 (.A(A), .B(B), .out_3(n20_bit_slt_1_out_3));
  _20_bit_SLL u_20_bit_sll_1 (.inputs(A), .shamt(shamt), .\output (n20_bit_sll_1_output));
  Adder #(.width(20)) adder_2 (.a(A), .b(not_1_out), .out(adder_2_out), .cin(1'b1), .cout(adder_2_cout));
  assign and_1_out = A & B;  // AND_Gate and_1, 20 bits wide
  not not_2 (Subovf, adder_2_cout);
  Multiplexer #(.select(3), .width(20), .enable("false")) multiplexer_1 (
    .in0(nor_1_out), .in1(or_1_out), .in2(adder_1_out), .in3(n20_bit_srl_1_output),
    .in4(n20_bit_slt_1_out_3), .in5(n20_bit_sll_1_output), .in6(adder_2_out), .in7(and_1_out),
    .out(\output ), .sel(select));
  ALU_control_unit alu_control_unit_1 (
    .FUNC(func), .ALUOP(ALU_OP), .PIN_0(select[0]), .PIN_1(select[1]), .PIN_2(select[2]));  // open: NOR
  Comparator #(.width(20)) comparator_1 (.a(\output ), .b({20{1'b0}}), .eq(zero));  // open: gt, lt
  Comparator #(.width(20)) comparator_2 (.a(A), .b(B), .gt(comparator_2_gt), .lt(comparator_2_lt));  // open: eq
  or or_2 (not_equal, comparator_2_gt, comparator_2_lt);
  Multiplexer #(.select(3), .enable("false")) multiplexer_2 (
    .in0(1'b0), .in1(1'b0), .in2(Addovf), .in3(1'b0), .in4(1'b0), .in5(1'b0), .in6(Subovf), .in7(1'b0),
    .out(overflow), .sel(select));

  // Notes on the sheet:
  //   ALU
  //   Group-11
  //   Najifa Tabassum - 2211578042
  //   Mohammed Arif Mainuddin - 2211577042
endmodule

module _20_bit_SRL (
  input  [19:0] Input,
  input  [1:0] shamt,
  output [19:0] \output 
);

  wire [4:0] bit_extender_1_out;

  assign bit_extender_1_out = {{3{1'b0}}, shamt};  // Bit_Extender bit_extender_1
  Shifter #(.width(20), .shift("lr")) shifter_1 (.in(Input), .\dist (bit_extender_1_out), .out(\output ));
endmodule

module _20_bit_SLT (
  input  [19:0] A,
  input  [19:0] B,
  output [19:0] out_3
);

  wire comparator_1_lt;

  Comparator #(.width(20)) comparator_1 (.a(A), .b(B), .lt(comparator_1_lt));  // open: gt, eq
  assign out_3 = {{19{1'b0}}, comparator_1_lt};  // Bit_Extender bit_extender_1
endmodule

module _20_bit_SLL (
  input  [19:0] inputs,
  input  [1:0] shamt,
  output [19:0] \output 
);

  wire [4:0] bit_extender_1_out;

  assign bit_extender_1_out = {{3{1'b0}}, shamt};  // Bit_Extender bit_extender_1
  Shifter #(.width(20)) shifter_1 (.in(inputs), .\dist (bit_extender_1_out), .out(\output ));
endmodule

module ALU_control_unit (
  input  [1:0] ALUOP,
  input  [2:0] FUNC,
  output NOR,
  output PIN_0,
  output PIN_1,
  output PIN_2
);

  wire and_1_out, and_2_out, and_4_out, and_5_out, and_6_out, and_7_out, and_8_out, decoder_1_out0,
       decoder_1_out1, decoder_1_out2, decoder_1_out3, decoder_1_out4, decoder_1_out5, decoder_1_out6,
       decoder_1_out7, decoder_2_out0, decoder_2_out1, decoder_2_out2, decoder_2_out3, or_1_out, or_2_out;

  Decoder #(.select(3), .enable("false")) decoder_1 (
    .out0(decoder_1_out0), .out1(decoder_1_out1), .out2(decoder_1_out2), .out3(decoder_1_out3),
    .out4(decoder_1_out4), .out5(decoder_1_out5), .out6(decoder_1_out6), .out7(decoder_1_out7), .sel(FUNC));
  Decoder #(.select(2), .enable("false")) decoder_2 (
    .out0(decoder_2_out0), .out1(decoder_2_out1), .out2(decoder_2_out2), .out3(decoder_2_out3), .sel(ALUOP));
  and and_1 (and_1_out, decoder_2_out2, decoder_1_out2);
  and and_2 (and_2_out, decoder_2_out2, decoder_1_out6);
  and and_3 (NOR, decoder_2_out2, decoder_1_out0);
  and and_4 (and_4_out, decoder_2_out2, decoder_1_out1);
  or or_1 (or_1_out, and_1_out, decoder_2_out1);
  and and_5 (and_5_out, decoder_2_out2, decoder_1_out3);
  and and_6 (and_6_out, decoder_2_out2, decoder_1_out4);
  and and_7 (and_7_out, decoder_2_out2, decoder_1_out5);
  or or_2 (or_2_out, and_2_out, decoder_2_out0);
  and and_8 (and_8_out, decoder_2_out2, decoder_1_out7);
  or or_3 (PIN_0, and_4_out, and_5_out, and_7_out, and_8_out);
  or or_4 (PIN_1, or_1_out, and_5_out, or_2_out, and_8_out);
  or or_5 (PIN_2, and_6_out, and_7_out, or_2_out, and_8_out);

  // Notes on the sheet:
  //   OR
  //   ADD
  //   SRL
  //   SLT
  //   SLL
  //   SUB
  //   AND
  //   SUB/BEQ
  //   ALU Control Unit
  //   Group-11
  //   Najifa Tabassum - 2211578042
  //   Mohammed Arif Mainuddin - 2211577042
endmodule

module control_unit (
  input  [2:0] Opcode,
  output RegDest,
  output Beq,
  output Bne,
  output Jump,
  output MemRead,
  output MemToReg,
  output MemWrite,
  output ALUsrc,
  output RegWrite,
  output [1:0] ALUop
);

  wire decoder_1_out6;

  Decoder #(.select(3), .enable("false")) decoder_1 (
    .out0(ALUop[1]), .out1(Beq), .out2(Bne), .out3(MemWrite), .out4(Jump), .out5(MemRead),
    .out6(decoder_1_out6), .sel(Opcode));  // open: out7
  or or_1 (ALUop[0], MemWrite, MemRead, decoder_1_out6);
  or or_2 (ALUsrc, MemWrite, MemRead, decoder_1_out6);
  or or_3 (RegWrite, ALUop[1], MemRead, decoder_1_out6);

  assign MemToReg = MemRead;
  assign RegDest = ALUop[1];

  // Notes on the sheet:
  //   Control Unit
  //   Group-11
  //   Najifa Tabassum - 2211578042
  //   Mohammed Arif Mainuddin - 2211577042
endmodule

module _20_bit_cpu (
);

  wire ALUSrc, and_1_out, and_2_out, Beq, beq_out, Bne, bne_out, branch_out, clk, clr, Jump,
       main_1_not_equal, main_1_zero, MemRead, MemToReg, MemWrite, RegDest, RegWrite, reset, reset_out, stop;
  wire [1:0] ALUOP;
  wire [3:0] _0, _1, _2, _3, _4, I0, I1, I2, I3, I4, multiplexer_1_out;
  wire [19:0] adder_1_out, BranchAddr, JumpAddr, main_1_output, multiplexer_2_out, multiplexer_3_out,
       multiplexer_5_out, n20_bit_reg_1_read_data_1, n20_bit_reg_1_read_data_2, pc_1_pcout, ram_1_data;

  Clock u_clk (.out(clk));
  Hex_Digit_Display hex_digit_display_1 (.value(_4));  // open: dp
  PC pc_1 (.PCin(multiplexer_5_out), .PCout(pc_1_pcout), .clk(clk), .reset(reset_out));
  Button u_reset (.out(reset_out));
  Hex_Digit_Display hex_digit_display_2 (.value(_3));  // open: dp
  nop nop_1 (.in_1({I4, I3, I2, I1, I0}), .out_2(stop));
  Button reg_reset (.out(reset));
  Hex_Digit_Display hex_digit_display_3 (.value(_2));  // open: dp
  Hex_Digit_Display hex_digit_display_4 (.value(_1));  // open: dp
  Adder #(.width(20)) adder_1 (.a(20'h1), .b(pc_1_pcout), .out(adder_1_out));  // open: cin, cout
  ROM #(.addrWidth(20), .dataWidth(20)) rom_1 (.addr(pc_1_pcout), .data({I4, I3, I2, I1, I0}));  // open: sel
  Button mem_clr (.out(clr));
  Hex_Digit_Display hex_digit_display_5 (.value(_0));  // open: dp
  Hex_Digit_Display hex_digit_display_6 (.value(I4));  // open: dp
  Hex_Digit_Display hex_digit_display_7 (.value(I3));  // open: dp
  assign JumpAddr = {{3{1'b0}}, {I4[0], I3, I2, I1, I0}};  // Bit_Extender bit_extender_1
  Hex_Digit_Display hex_digit_display_8 (.value(I2));  // open: dp
  Hex_Digit_Display hex_digit_display_9 (.value(I0));  // open: dp
  Hex_Digit_Display hex_digit_display_10 (.value(I1));  // open: dp
  Multiplexer #(.width(4), .enable("false")) multiplexer_1 (
    .in0({I3[0], I2[3:1]}), .in1({I2[0], I1[3:1]}), .out(multiplexer_1_out), .sel(RegDest));
  and and_1 (and_1_out, ~stop, RegWrite);  // AND_Gate
  assign BranchAddr = {{11{1'b0}}, {I2[0], I1, I0}};  // Bit_Extender bit_extender_2
  control_unit control_unit_1 (
    .Opcode(I4[3:1]), .RegDest(RegDest), .Beq(Beq), .Jump(Jump), .MemRead(MemRead), .MemToReg(MemToReg),
    .MemWrite(MemWrite), .ALUsrc(ALUSrc), .RegWrite(RegWrite), .ALUop(ALUOP), .Bne(Bne));
  _20_bit_reg u_20_bit_reg_1 (
    .Read_Data_1(n20_bit_reg_1_read_data_1), .Read_Register_1({I4[0], I3[3:1]}),
    .Write_Register(multiplexer_1_out), .Read_Data_2(n20_bit_reg_1_read_data_2),
    .Read_Register__2({I3[0], I2[3:1]}), .Write_Control(and_1_out), .Write_Data({_4, _3, _2, _1, _0}),
    .Clear(reset), .clk(clk));
  Multiplexer #(.width(20), .enable("false")) multiplexer_2 (
    .in0(n20_bit_reg_1_read_data_2), .in1(BranchAddr), .out(multiplexer_2_out), .sel(ALUSrc));
  main main_1 (
    .func(I0[2:0]), .\output (main_1_output), .zero(main_1_zero), .A(n20_bit_reg_1_read_data_1),
    .B(multiplexer_2_out), .shamt({I1[0], I0[3]}), .ALU_OP(ALUOP), .not_equal(main_1_not_equal));  // open: overflow
  and u_beq (beq_out, Beq, main_1_zero);
  and u_bne (bne_out, Bne, main_1_not_equal);
  and and_2 (and_2_out, ~stop, 1'b1);  // AND_Gate
  Multiplexer #(.width(20), .enable("false")) multiplexer_3 (
    .in0(adder_1_out), .in1(BranchAddr), .out(multiplexer_3_out), .sel(branch_out));
  or branch (branch_out, beq_out, bne_out);
  RAM #(.addrWidth(20), .dataWidth(20), .bus("separate")) ram_1 (
    .addr(main_1_output), .din(n20_bit_reg_1_read_data_2), .data(ram_1_data), .str(MemWrite),
    .sel(and_2_out), .clk(clk), .ld(MemRead), .clr(clr));
  Multiplexer #(.width(20), .enable("false")) multiplexer_4 (
    .in0(main_1_output), .in1(ram_1_data), .out({_4, _3, _2, _1, _0}), .sel(MemToReg));
  Multiplexer #(.width(20), .enable("false")) multiplexer_5 (
    .in0(multiplexer_3_out), .in1(JumpAddr), .out(multiplexer_5_out), .sel(Jump));

  // Other names for the same wires on the sheet: ins[19:0] = {I4, I3, I2, I1, I0}

  // Notes on the sheet:
  //   CPU
  //   Group-11
  //   Write Data
  //   Najifa Tabassum - 2211578042
  //   Mohammed Arif Mainuddin - 2211577042
  //   contents of rom_1 (hex, n*v repeats v):
  //   a0201 c0405 a0601 22407 6262 c2201 80003 c0804 28a4 c0c01 40c0c 6266 c6601 60f5 6113 6326 0 60e02
  //   60603 61004 61205
  //   Ins Data
  //   func
  //   shamt
  //   rd
  //   rt
  //   rs
  //   opcode
  //   imm
endmodule

module _20_bit_reg (
  input  [3:0] Read_Register_1,
  input  [3:0] Write_Register,
  input  [3:0] Read_Register__2,
  input  Write_Control,
  input  [19:0] Write_Data,
  input  Clear,
  input  clk,
  output [19:0] Read_Data_1,
  output [19:0] Read_Data_2
);

  wire and_1_out, and_2_out, and_3_out, and_4_out, and_5_out, and_6_out, and_7_out, and_8_out, and_9_out,
       and_10_out, and_11_out, and_12_out, and_13_out, and_14_out, and_15_out, and_16_out, decoder_1_out0,
       decoder_1_out1, decoder_1_out2, decoder_1_out3, decoder_1_out4, decoder_1_out5, decoder_1_out6,
       decoder_1_out7, decoder_1_out8, decoder_1_out9, decoder_1_out10, decoder_1_out11, decoder_1_out12,
       decoder_1_out13, decoder_1_out14, decoder_1_out15;
  wire [19:0] _0_q, _1_q, _2_q, _3_q, _4_q, _5_q, _6_q, _7_q, _8_q, _9_q, _10_q, _11_q, _12_q, _13_q, _14_q,
       _15_q;

  Decoder #(.select(4), .enable("false")) decoder_1 (
    .out0(decoder_1_out0), .out1(decoder_1_out1), .out2(decoder_1_out2), .out3(decoder_1_out3),
    .out4(decoder_1_out4), .out5(decoder_1_out5), .out6(decoder_1_out6), .out7(decoder_1_out7),
    .out8(decoder_1_out8), .out9(decoder_1_out9), .out10(decoder_1_out10), .out11(decoder_1_out11),
    .out12(decoder_1_out12), .out13(decoder_1_out13), .out14(decoder_1_out14), .out15(decoder_1_out15),
    .sel(Write_Register));
  and and_1 (and_1_out, decoder_1_out0, Write_Control);
  and and_2 (and_2_out, decoder_1_out1, Write_Control);
  and and_3 (and_3_out, decoder_1_out2, Write_Control);
  and and_4 (and_4_out, decoder_1_out3, Write_Control);
  and and_5 (and_5_out, decoder_1_out4, Write_Control);
  and and_6 (and_6_out, decoder_1_out5, Write_Control);
  and and_7 (and_7_out, decoder_1_out6, Write_Control);
  and and_8 (and_8_out, decoder_1_out7, Write_Control);
  Register #(.width(20)) _0 (.D(Write_Data), .en(and_1_out), .Q(_0_q), .clk(clk), .clr(Clear));
  Register #(.width(20)) _1 (.D(Write_Data), .en(and_2_out), .Q(_1_q), .clk(clk), .clr(Clear));
  Register #(.width(20)) _2 (.D(Write_Data), .en(and_3_out), .Q(_2_q), .clk(clk), .clr(Clear));
  Register #(.width(20)) _3 (.D(Write_Data), .en(and_4_out), .Q(_3_q), .clk(clk), .clr(Clear));
  Register #(.width(20)) _4 (.D(Write_Data), .en(and_5_out), .Q(_4_q), .clk(clk), .clr(Clear));
  Register #(.width(20)) _5 (.D(Write_Data), .en(and_6_out), .Q(_5_q), .clk(clk), .clr(Clear));
  Register #(.width(20)) _6 (.D(Write_Data), .en(and_7_out), .Q(_6_q), .clk(clk), .clr(Clear));
  Register #(.width(20)) _7 (.D(Write_Data), .en(and_8_out), .Q(_7_q), .clk(clk), .clr(Clear));
  and and_9 (and_9_out, decoder_1_out8, Write_Control);
  and and_10 (and_10_out, decoder_1_out9, Write_Control);
  and and_11 (and_11_out, decoder_1_out10, Write_Control);
  and and_12 (and_12_out, decoder_1_out11, Write_Control);
  and and_13 (and_13_out, decoder_1_out12, Write_Control);
  and and_14 (and_14_out, decoder_1_out13, Write_Control);
  and and_15 (and_15_out, decoder_1_out14, Write_Control);
  and and_16 (and_16_out, decoder_1_out15, Write_Control);
  Register #(.width(20)) _8 (.D(Write_Data), .en(and_9_out), .Q(_8_q), .clk(clk), .clr(Clear));
  Register #(.width(20)) _9 (.D(Write_Data), .en(and_10_out), .Q(_9_q), .clk(clk), .clr(Clear));
  Register #(.width(20)) _10 (.D(Write_Data), .en(and_11_out), .Q(_10_q), .clk(clk), .clr(Clear));
  Register #(.width(20)) _11 (.D(Write_Data), .en(and_12_out), .Q(_11_q), .clk(clk), .clr(Clear));
  Register #(.width(20)) _12 (.D(Write_Data), .en(and_13_out), .Q(_12_q), .clk(clk), .clr(Clear));
  Register #(.width(20)) _13 (.D(Write_Data), .en(and_14_out), .Q(_13_q), .clk(clk), .clr(Clear));
  Register #(.width(20)) _14 (.D(Write_Data), .en(and_15_out), .Q(_14_q), .clk(clk), .clr(Clear));
  Register #(.width(20)) _15 (.D(Write_Data), .en(and_16_out), .Q(_15_q), .clk(clk), .clr(Clear));
  Multiplexer #(.select(4), .width(20), .enable("false")) multiplexer_1 (
    .in0(_0_q), .in1(_1_q), .in2(_2_q), .in3(_3_q), .in4(_4_q), .in5(_5_q), .in6(_6_q), .in7(_7_q),
    .in8(_8_q), .in9(_9_q), .in10(_10_q), .in11(_11_q), .in12(_12_q), .in13(_13_q), .in14(_14_q),
    .in15(_15_q), .out(Read_Data_1), .sel(Read_Register_1));
  Multiplexer #(.select(4), .width(20), .enable("false")) multiplexer_2 (
    .in0(_0_q), .in1(_1_q), .in2(_2_q), .in3(_3_q), .in4(_4_q), .in5(_5_q), .in6(_6_q), .in7(_7_q),
    .in8(_8_q), .in9(_9_q), .in10(_10_q), .in11(_11_q), .in12(_12_q), .in13(_13_q), .in14(_14_q),
    .in15(_15_q), .out(Read_Data_2), .sel(Read_Register__2));

  // Notes on the sheet:
  //   Mohammed Arif Mainuddin
  //   2211577024
  //   Najifa Tabassum
  //   2211578042
endmodule

module PC (
  input  [19:0] PCin,
  input  clk,
  input  reset,
  output [19:0] PCout
);

  Register #(.width(20)) register_1 (.D(PCin), .Q(PCout), .clk(clk), .clr(reset));  // open: en
endmodule

module nop (
  input  [19:0] in_1,
  output out_2
);

  Comparator #(.width(20)) comparator_1 (.a(in_1), .b({20{1'b0}}), .eq(out_2));  // open: gt, lt
endmodule
