// Logisim project control_unit.circ as structural Verilog
module control_unit (
  input  [2:0] Opcode,
  output RegDest,
  output Branch,
  output Jump,
  output MemRead,
  output MemToReg,
  output MemWrite,
  output ALUsrc,
  output RegWrite,
  output [1:0] ALUop
);

  wire decoder_1_out1, decoder_1_out2, decoder_1_out6;

  Decoder #(.select(3), .enable("false")) decoder_1 (
    .out0(ALUop[1]), .out1(decoder_1_out1), .out2(decoder_1_out2), .out3(MemWrite), .out4(Jump),
    .out5(MemRead), .out6(decoder_1_out6), .sel(Opcode));  // open: out7
  or or_1 (ALUop[0], decoder_1_out2, MemRead, decoder_1_out6);
  or or_2 (Branch, decoder_1_out1, decoder_1_out2);
  or or_3 (ALUsrc, decoder_1_out1, decoder_1_out2, MemWrite, MemRead, decoder_1_out6);
  or or_4 (RegWrite, ALUop[1], MemRead, decoder_1_out6);

  assign MemToReg = MemRead;
  assign RegDest = ALUop[1];
endmodule
