// Logisim project project_practice.circ as structural Verilog: 4 circuits, main circuit main
module main (
  input  Cin,
  input  [19:0] A,
  input  [19:0] B,
  input  [4:0] shamt
);

  wire not_1_out;
  wire [19:0] not_2_out;

  not not_1 (not_1_out, Cin);
  assign not_2_out = ~B;  // NOT_Gate not_2, 20 bits wide
  // NOR_Gate nor_1 has open pins: in0=A, in1=B, out=open
  // OR_Gate or_1 has open pins: in0=A, in1=B, out=open
  Adder #(.width(20)) adder_1 (.a(A), .b(B), .cin(Cin));  // open: out, cout
  _20_bit_SRL u_20_bit_srl_1 (.Input(A), .shamt(shamt));  // open: output
  _20_bit_SLT u_20_bit_slt_1 (.A(A), .B(B));  // open: out_3
  _20_bit_SLL u_20_bit_sll_1 (.inputs(A), .shamt(shamt));  // open: output
  Adder #(.width(20)) adder_2 (.a(A), .b(not_2_out), .cin(not_1_out));  // open: out, cout
  // AND_Gate and_1 has open pins: in0=A, in1=B, out=open
endmodule

module _20_bit_SRL (
  input  [19:0] Input,
  input  [4:0] shamt,
  output [19:0] \output 
);

  Shifter #(.width(20), .shift("lr")) shifter_1 (.in(Input), .\dist (shamt), .out(\output ));
endmodule

module _20_bit_SLT (
  input  [19:0] A,
  input  [19:0] B,
  output [19:0] out_3
);

  wire comparator_1_lt;

  Comparator #(.width(20)) comparator_1 (.a(A), .b(B), .lt(comparator_1_lt));  // open: gt, eq
  assign out_3 = {{19{1'b0}}, comparator_1_lt};  // Bit_Extender bit_extender_1
endmodule

module _20_bit_SLL (
  input  [19:0] inputs,
  input  [4:0] shamt,
  output [19:0] \output 
);

  Shifter #(.width(20)) shifter_1 (.in(inputs), .\dist (shamt), .out(\output ));
endmodule
